# Fritzing sketch schematic (saved by Fritzing 0.9.3b)
breadboards: 1

parts:
  Bauteil1 = Arduino Uno (Rev3)
  R1 = Resistor [tolerance=±5% resistance=4.7k package="1206 [SMD]"]
  R2 = Resistor [tolerance=±5% resistance=10k package="1206 [SMD]"]
  GY-NEO6MV2 = SUP500F [package=sup500f]
  S1 = Taiway 100-SP-X-T1 SPDT Miniature Toggle Switch [part_number=100-SP-X-T1-0-0-B1-M1 package=THT]
  Componente1 = XBee Explorer Regulated
  VCC1 = Battery block 9V
  R3 = Resistor [tolerance=±5% resistance=220 package="0402 [SMD]"]

nets:
  N1: Bauteil1.A0, S1.L1
  GND: Bauteil1.GND, R2.Pin_1, GY-NEO6MV2.RX-I, Componente1.GND, VCC1.-, R3.Pin_0
  N2: Bauteil1.D3_PWM, GY-NEO6MV2.VCC
  N3: Bauteil1.D4, R1.Pin_0
  N4: Bauteil1.D5_PWM, Componente1.DOUT
  N5: Bauteil1.D6_PWM, Componente1.DIN
  5V: Bauteil1.5V, GY-NEO6MV2.TX-O, S1.COM, Componente1.5V
  N6: Bauteil1.VIN, VCC1.+
  N7: R1.Pin_1, R2.Pin_0, GY-NEO6MV2.GND
  N8: S1.L2, R3.Pin_1

notes:
  GND: Black
  VCC: Red
  RX: Yellow
  TX: Green
